// Logisim project edge_detector.circ as structural Verilog: 1 circuit, main circuit main
module main (
);

  wire button_1_out, clock_1_out, d_ff_1_q, d_ff_1_qn, d_ff_2_q, d_ff_2_qn, FALLING, RISING;

  Clock clock_1 (.out(clock_1_out));
  Button button_1 (.out(button_1_out));
  // Digital_Oscilloscope #(.nState(29)) digital_oscilloscope_1: pin names not known; wires that end beside it: clock_1_out, button_1_out, RISING, FALLING
  D_Flip_Flop d_ff_1 (.D(button_1_out), .clk(clock_1_out), .Q(d_ff_1_q), .Qn(d_ff_1_qn));  // open: preset, reset
  D_Flip_Flop d_ff_2 (.D(d_ff_1_q), .clk(clock_1_out), .Q(d_ff_2_q), .Qn(d_ff_2_qn));  // open: preset, reset
  and and_1 (FALLING, d_ff_1_qn, d_ff_2_q);
  and and_2 (RISING, d_ff_1_q, d_ff_2_qn);
endmodule
